# Fritzing sketch NanoModulo (saved by Fritzing 0.8.5b)
breadboards: 1

parts:
  J1 = Basic Servo
  Composants1 = Arduino Nano (Rev3.0)

nets:
  GND: J1.gnd, Composants1.GND
  VCC: J1.vcc, Composants1.5V
  N1: J1.pulse, Composants1.D3
