# Fritzing sketch robomodo (saved by Fritzing 0.8.7b)

parts:
  Composant1 = Arduino Fio (Funnel I/O)
  VCC1 = Battery  # not connected
  J1 = Basic Servo
  U1 = XBee

nets:
  VCC: Composant1.VCC, J1.vcc, U1.pin20
  GND: Composant1.GND, J1.gnd, U1.pin19
  N1: Composant1.D5_PWM, J1.pulse
  N2: Composant1.D0/RXI, U1.pin13
  N3: Composant1.D1/TXO, U1.pin17
